# Fritzing sketch sensor-rail-mini-mint (saved by Fritzing 0.9.3b)
breadboards: 6

parts:
  IC3 = MCP23017 I2C I/O Expander
  Part35 = Adafruit TCA9548A
  U13 = Molex Picoblade Series Header [part_number=0533980371 package=Picoblade-53398-0371]
  U12 = Molex Picoblade Series Header [part_number=0533980671 package=Picoblade-53398-0671]
  Part37 = Adafruit TSL2591 [part_number="Adafruit #1980"]
  Part38 = Adafruit VEML6075 UV Sensor Breakout [part_number=3964]
  Part39 = Adafruit TCS34725 RGB Color Sensor [part_number="Adafruit #1334"]
  Part41 = Adafruit TSL2591 [part_number="Adafruit #1980"]
  Part42 = Adafruit VEML6075 UV Sensor Breakout [part_number=3964]
  U14 = Molex Picoblade Series Header [part_number=0533980671 package=Picoblade-53398-0671]
  U15 = Molex Picoblade Series Header [part_number=0533980371 package=Picoblade-53398-0371]
  Part43 = Adafruit TCS34725 RGB Color Sensor [part_number="Adafruit #1334"]
  U16 = MLX90614 [package=to-39]
  Part45 = Adafruit VL6180X Time of Flight Distance Sensor [part_number="Adafruit #3316"]
  U18 = Molex Picoblade Series Header [part_number=0533980471 package=Picoblade-53398-0471]
  R3 = Resistor [tolerance=±5% resistance=10k package=THT]
  R4 = Resistor [tolerance=±5% resistance=10k package=THT]
  Part46 = Adafruit SHT31-D Sensirion Temperature/Humidity Sensor [part_number="Adafruit #2857"]
  Part47 = Adafruit SGP30 Gas Sensor
  Part48 = Adafruit MLX90393 Magnetometer [part_number="Adafruit #4022"]
  Part49 = 9-DOF Absolute Orientation IMU Fusion Breakout - BNO055
  U17 = Molex Picoblade Series Header [part_number=0533980571 package=Picoblade-53398-0571]
  Q1 = Basic FET N-Channel [package="TO220 [THT]"]
  U19 = Molex Picoblade Series Header [part_number=0533980871 package=Picoblade-53398-0871]
  U20 = Molex Picoblade Series Header [part_number=0533980271 package=Picoblade-53398-0271]

nets:
  N1: IC3.GPB0, U17.1
  N2: IC3.GPB1, R3.Pin_0, U17.2
  N3: IC3.GPB2, R4.Pin_0, U17.3
  N4: IC3.GPB3, Part45.GPIO, U17.4
  N5: IC3.GPB4, Part45.XSHUT, U17.5
  N6: IC3.GPB5, Part46.ALERT
  N7: IC3.GPB6, Part49.RST_5V
  N8: IC3.GPB7, Part49.INT_3V
  VIN: IC3.VDD, Part35.VCC, U12.6, Part38.VIN, Part39.VIN, Part42.VIN, U14.6, Part43.VIN, U16.VDD, Part45.VIN, U18.4, Part46.VIN, Part47.VIN, Part48.VIN, Part49.5.0V, Q1.drain
  GND: IC3.VSS, Part35.GND, U12.5, Part39.GND, U14.5, Part43.GND, U16.VSS, Part45.GND, U18.3, Part46.GND, Part47.GND, Part48.GND, Part49.GND, U19.2
  N9: IC3.SCL, Part35.INPUTSCL, U19.8, U20.2
  N10: IC3.SDA, Part35.INPUTSDA, U19.7, U20.1
  N11: IC3.INTB, U19.5
  N12: IC3.INTA, U19.4
  N13: IC3.GPA0, Part48.INT_3V
  N14: IC3.GPA1, Part41.INT, U15.1
  N15: IC3.GPA2, U15.2, Part43.INT
  N16: IC3.GPA3, U15.3, Part43.LED_EN
  N17: IC3.GPA4, U13.1, Part37.INT
  N18: IC3.GPA5, U13.2, Part39.INT
  N19: IC3.GPA6, U13.3, Part39.LED_EN
  N20: Part35.2SDA, U12.1, Part37.SDA, Part38.SDA
  N21: Part35.2SCL, U12.2, Part37.SCL, Part38.SCL
  N22: Part35.3SDA, U12.3, Part39.SDA
  N23: Part35.3SCL, U12.4, Part39.SCL
  N24: Part35.4SDA, Part41.SDA, Part42.SDA, U14.1
  N25: Part35.4SCL, Part41.SCL, Part42.SCL, U14.2
  N26: Part35.5SDA, U14.3, Part43.SDA
  N27: Part35.5SCL, U14.4, Part43.SCL
  N28: Part35.6SDA, Part49.SDA_5V
  N29: Part35.6SCL, Part49.SCL_5V
  N30: Part35.7SDA, Part48.SDA
  N31: Part35.7SCL, Part48.SCL
  N32: Part35.RESET, U19.6
  N33: Part35.0SDA, Part46.SDA, Part47.SDA
  N34: Part35.0SCL, Part46.SCL, Part47.SCL
  N35: Part35.1SDA, Part45.SDA, U18.1
  N36: Part35.1SCL, Part45.SCL, U18.2
  N37: U16.SCL_VZ, R4.Pin_1
  N38: U16.PWM_SDA, R3.Pin_1
  N39: Q1.gate, U19.1
  N40: Q1.source, U19.3

custom parts:
  MCP23017 I2C I/O Expander: The MCP23017 uses two i2c pins (these can be shared with other i2c devices), and in exchange gives you 16 general purpose pins. You can set each of 16 pins to be input, output, input with a pullup or open drain. There's even the ability to get an interrupt via an external pin when any of the inputs change so you don't have to keep polling the chip.
  Adafruit TCA9548A: You just found the perfect I2C sensor, and you want to wire up two or three or more of them to your Arduino when you realize "Uh oh, this chip has a fixed I2C address, and from what I know about I2C, you cannot have two devices with the same address on the same SDA/SCL pins!" Are you out of luck? You would be, if you didn't have this ultra-cool TCA9548A 1-to-8 I2C multiplexer! Finally, a way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
  Adafruit TSL2591: When the future is dazzlingly-bright, this ultra-high-range luminosity sensor will help you measure it. The TSL2591 luminosity sensor is an advanced digital light sensor, ideal for use in a wide range of light situations. Compared to low cost CdS cells, this sensor is more precise, allowing for exact lux calculations and can be configured for different gain/timing ranges to detect light ranges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
  Adafruit VEML6075 UV Sensor Breakout: This little sensor is a great way to add UVA and UVB light sensing to any microcontroller project. The VEML6075 from Vishay has both true UVA and UVB band light sensors and an I2C-controlled ADC that will take readings and integrate them. The sensor also comes with calibration registers so you can easily convert the UVA/UVB readings into the UV Index. Compared to our other UV sensors, this one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
  Adafruit TCS34725 RGB Color Sensor: Your electronics can now see in dazzling color with this lovely color light sensor. We found the best color sensor on the market, the TCS34725, which has RGB and Clear light sensing elements. An IR blocking filter, integrated on-chip and localized to the color sensing photodiodes, minimizes the IR spectral component of the incoming light and allows color measurements to be made accurately. The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
  Adafruit VL6180X Time of Flight Distance Sensor: The VL6180X is a Time of Flight distance sensor like no other you've used! The sensor contains a very tiny invisible laser source, and a matching sensor. The VL6180X can detect the "time of flight", or how long the light has taken to bounce back to the sensor. Since it uses a very narrow light source, it is good for determining distance of only the surface directly in front of it. Unlike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
  Adafruit SHT31-D Sensirion Temperature/Humidity Sensor: Sensirion Temperature/Humidity sensors are some of the finest & highest-accuracy devices you can get. And, finally we have some that have a true I2C interface for easy reading. The SHT31-D sensor has an excellent ±2% relative humidity and ±0.3°C accuracy for most uses. Unlike earlier SHT sensors, this sensor has a true I2C interface, and (bonus!) even with two address options. It also is 3V or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
  9-DOF Absolute Orientation IMU Fusion Breakout - BNO055: A MEMS accelerometer, magnetometer and gyroscope on a single die with a high speed ARM Cortex-M0 based processor to digest all the sensor data, abstract the sensor fusion and real time requirements away, and spit out data you can use in quaternions, Euler angles or vectors.
